# Fritzing sketch keypad (saved by Fritzing 0.9.0b)
breadboards: 1

parts:
  KEYPAD1 = Membrane Matrix Keypad
  Part1 = Arduino Uno (Rev3)
  J1 = Basic Servo
  R1 = Resistor [tolerance=±5% resistance=1k package=THT]
  R2 = Resistor [tolerance=±5% resistance=1k package=THT]
  Q1 = NPN-Transistor [package="SOT-23 [SMD]"]
  J3 = Piezo Speaker

nets:
  N1: KEYPAD1.1, Part1.D10_PWM/SS, Part1.D11_PWM/MOSI, J1.pulse
  N2: KEYPAD1.2, Part1.D4
  N3: KEYPAD1.3, Part1.D9_PWM
  N4: KEYPAD1.4, Part1.D8
  N5: KEYPAD1.5, Part1.D7
  N6: KEYPAD1.6, Part1.D6_PWM
  N7: KEYPAD1.7, Part1.D5_PWM
  GND: Part1.GND, J1.gnd
  N8: Part1.D2, R1.Pin_0
  5V: Part1.5V, J1.vcc
  N9: R2.Pin_1, Q1.1, J3.pin1
  GND_2: Q1.2
  5V_2: J3.pin2

custom parts:
  Membrane Matrix Keypad: Membrane Matrix 3x4 Keypad
